// Logisim project cpu.circ as structural Verilog: 24 circuits, main circuit main
module main (
  input  [3:0] in_1,
  input  [15:0] in_2,
  output out_3
);

  wire undriven;
  wire [3:0] register16_1_d_out, undriven_5;
  wire [15:0] alu_1_result, instruction_memory_1_data_out1, registerfile16_1_data_out1, undriven_2,
       undriven_3, undriven_4;
  wire [15:4] register16_1_d_out_2;

  instruction_memory instruction_memory_1 (
    .read_addr1(register16_1_d_out), .write_addr(in_1), .data_out1(instruction_memory_1_data_out1));
  register16 register16_1 (.D_OUT({register16_1_d_out_2, register16_1_d_out}));  // open: WE, D_IN, CLK, OE
  RegisterFile16 registerfile16_1 (
    .data_in(undriven_2), .write_addr(register16_1_d_out_2[11:8]), .LD(undriven),
    .data_out1(registerfile16_1_data_out1));  // open: read_addr1, read_addr2, data_out2
  ALU alu_1 (.Operation(undriven_5), .IN_A(undriven_3), .IN_B(undriven_4), .Out_Carry(out_3), .Result(alu_1_result));

  // Notes on the sheet:
  //   Fetch the instruction
  //   Instruction Memory
  //   Program Counter
  //   Data Memory
endmodule

module full_adder (
  input  IN_A,
  input  IN_B,
  input  IN_Carry,
  output Out_Carry,
  output Sum
);

  wire and_1_out, and_2_out, and_3_out;

  and and_1 (and_1_out, IN_A, IN_B);
  and and_2 (and_2_out, IN_A, IN_Carry);
  and and_3 (and_3_out, IN_B, IN_Carry);
  xor xor_1 (Sum, IN_A, IN_B, IN_Carry);
  or or_1 (Out_Carry, and_1_out, and_2_out, and_3_out);
endmodule

module adder4 (
  input  [3:0] IN_A,
  input  [3:0] IN_B,
  input  IN_Carry,
  output Out_Carry,
  output b3,
  output b2,
  output b1,
  output b0
);

  wire full_adder_2_out_carry, full_adder_3_out_carry, full_adder_4_out_carry;

  full_adder full_adder_1 (
    .IN_A(IN_A[3]), .IN_B(IN_B[3]), .IN_Carry(full_adder_2_out_carry), .Out_Carry(Out_Carry), .Sum(b3));
  full_adder full_adder_2 (
    .IN_A(IN_A[2]), .IN_B(IN_B[2]), .IN_Carry(full_adder_3_out_carry), .Out_Carry(full_adder_2_out_carry),
    .Sum(b2));
  full_adder full_adder_3 (
    .IN_A(IN_A[1]), .IN_B(IN_B[1]), .IN_Carry(full_adder_4_out_carry), .Out_Carry(full_adder_3_out_carry),
    .Sum(b1));
  full_adder full_adder_4 (
    .IN_A(IN_A[0]), .IN_B(IN_B[0]), .IN_Carry(IN_Carry), .Out_Carry(full_adder_4_out_carry), .Sum(b0));
endmodule

module adder16 (
  input  [15:0] IN_A,
  input  [15:0] IN_B,
  input  IN_Carry,
  output Out_Carry,
  output [15:0] Sum
);

  wire adder4_2_out_carry, adder4_3_out_carry, adder4_4_out_carry;

  adder4 adder4_1 (
    .IN_A(IN_A[15:12]), .IN_B(IN_B[15:12]), .IN_Carry(adder4_2_out_carry), .Out_Carry(Out_Carry),
    .b3(Sum[15]), .b2(Sum[14]), .b1(Sum[13]), .b0(Sum[12]));
  adder4 adder4_2 (
    .IN_A(IN_A[11:8]), .IN_B(IN_B[11:8]), .IN_Carry(adder4_3_out_carry), .Out_Carry(adder4_2_out_carry),
    .b3(Sum[11]), .b2(Sum[10]), .b1(Sum[9]), .b0(Sum[8]));
  adder4 adder4_3 (
    .IN_A(IN_A[7:4]), .IN_B(IN_B[7:4]), .IN_Carry(adder4_4_out_carry), .Out_Carry(adder4_3_out_carry),
    .b3(Sum[7]), .b2(Sum[6]), .b1(Sum[5]), .b0(Sum[4]));
  adder4 adder4_4 (
    .IN_A(IN_A[3:0]), .IN_B(IN_B[3:0]), .IN_Carry(IN_Carry), .Out_Carry(adder4_4_out_carry), .b3(Sum[3]),
    .b2(Sum[2]), .b1(Sum[1]), .b0(Sum[0]));
endmodule

module subtractor16 (
  input  [15:0] IN_A,
  input  [15:0] IN_B,
  output [15:0] Sum
);

  wire [15:0] not_1_out;

  assign not_1_out = ~IN_B;  // NOT_Gate not_1, 16 bits wide
  adder16 adder16_1 (.IN_A(IN_A), .IN_B(not_1_out), .IN_Carry(1'b1), .Sum(Sum));  // open: Out_Carry
endmodule

module ALU (
  input  [3:0] Operation,
  input  [15:0] IN_A,
  input  [15:0] IN_B,
  output Out_Carry,
  output [15:0] Result
);

  wire [15:0] adder16_1_sum, and_1_out, left_bit_shifter16_1_result, not_1_out, or_1_out,
       right_bit_shifter16_1_result, subtractor16_1_sum;

  adder16 adder16_1 (.IN_A(IN_A), .IN_B(IN_B), .IN_Carry(1'b0), .Out_Carry(Out_Carry), .Sum(adder16_1_sum));
  subtractor16 subtractor16_1 (.IN_A(IN_A), .IN_B(IN_B), .Sum(subtractor16_1_sum));
  left_bit_shifter16 left_bit_shifter16_1 (.IN_A(IN_A), .Result(left_bit_shifter16_1_result));
  right_bit_shifter16 right_bit_shifter16_1 (.IN_A(IN_A), .Result(right_bit_shifter16_1_result));
  assign and_1_out = IN_A & IN_B;  // AND_Gate and_1, 16 bits wide
  assign or_1_out = IN_A | IN_B;  // OR_Gate or_1, 16 bits wide
  assign not_1_out = ~IN_A;  // NOT_Gate not_1, 16 bits wide
  multiplexer16x1 multiplexer16x1_1 (.out_18(Result));  // open: addr_in, IN_0, IN_1, IN_2, IN_3, IN_4, IN_5, IN_6, IN_7, IN_8, IN_9, IN_10, IN_11, IN_12, IN_13, IN_14, IN_15
endmodule

module left_bit_shifter16 (
  input  [15:0] IN_A,
  output [15:0] Result
);


  assign Result = {IN_A[14:0], 1'b0};
  // also tied to GND on the sheet: IN_A[15]
endmodule

module right_bit_shifter16 (
  input  [15:0] IN_A,
  output [15:0] Result
);


  assign Result = {1'b0, IN_A[15:1]};
  // also tied to GND on the sheet: IN_A[0]
endmodule

module decoder_8 (
  input  [2:0] IN_A,
  input  Clk,
  output Out_0,
  output Out_1,
  output Out_2,
  output Out_3,
  output Out_4,
  output Out_5,
  output Out_6,
  output Out_7
);

  and and_1 (Out_0, ~IN_A[2], ~IN_A[1], ~IN_A[0], Clk);  // AND_Gate
  and and_2 (Out_1, ~IN_A[2], ~IN_A[1], IN_A[0], Clk);  // AND_Gate
  and and_3 (Out_2, ~IN_A[2], IN_A[1], ~IN_A[0], Clk);  // AND_Gate
  and and_4 (Out_3, ~IN_A[2], IN_A[1], IN_A[0], Clk);  // AND_Gate
  and and_5 (Out_4, IN_A[2], ~IN_A[1], ~IN_A[0], Clk);  // AND_Gate
  and and_6 (Out_5, IN_A[2], ~IN_A[1], IN_A[0], Clk);  // AND_Gate
  and and_7 (Out_6, IN_A[2], IN_A[1], ~IN_A[0], Clk);  // AND_Gate
  and and_8 (Out_7, IN_A[2], IN_A[1], IN_A[0], Clk);
endmodule

module multiplexer16_8 (
  input  [2:0] Addr,
  input  [15:0] IN_0,
  input  [15:0] IN_1,
  input  [15:0] IN_2,
  input  [15:0] IN_3,
  input  [15:0] IN_4,
  input  [15:0] IN_5,
  input  [15:0] IN_6,
  input  [15:0] IN_7,
  output [15:0] Result
);

  wire decoder_8_1_out_0, decoder_8_1_out_1, decoder_8_1_out_2, decoder_8_1_out_3, decoder_8_1_out_4,
       decoder_8_1_out_5, decoder_8_1_out_6, decoder_8_1_out_7;

  decoder_8 decoder_8_1 (
    .IN_A(Addr), .Out_0(decoder_8_1_out_0), .Out_1(decoder_8_1_out_1), .Out_2(decoder_8_1_out_2),
    .Out_3(decoder_8_1_out_3), .Out_4(decoder_8_1_out_4), .Out_5(decoder_8_1_out_5),
    .Out_6(decoder_8_1_out_6), .Out_7(decoder_8_1_out_7));  // open: Clk
  assign Result = decoder_8_1_out_0 ? IN_0 : 16'bz;  // Controlled_Buffer controlled_buffer_1
  assign Result = decoder_8_1_out_1 ? IN_1 : 16'bz;  // Controlled_Buffer controlled_buffer_2
  assign Result = decoder_8_1_out_2 ? IN_2 : 16'bz;  // Controlled_Buffer controlled_buffer_3
  assign Result = decoder_8_1_out_3 ? IN_3 : 16'bz;  // Controlled_Buffer controlled_buffer_4
  assign Result = decoder_8_1_out_4 ? IN_4 : 16'bz;  // Controlled_Buffer controlled_buffer_5
  assign Result = decoder_8_1_out_5 ? IN_5 : 16'bz;  // Controlled_Buffer controlled_buffer_6
  assign Result = decoder_8_1_out_6 ? IN_6 : 16'bz;  // Controlled_Buffer controlled_buffer_7
  assign Result = decoder_8_1_out_7 ? IN_7 : 16'bz;  // Controlled_Buffer controlled_buffer_8
endmodule

module d_flip_flop (
  input  WE,
  input  CLK,
  input  D,
  input  OE,
  output Q
);

  wire and_1_out, and_2_out, and_3_out, nor_1_out, nor_2_out, not_1_out;

  and and_1 (and_1_out, WE, CLK);
  not not_1 (not_1_out, D);
  and and_2 (and_2_out, not_1_out, and_1_out);
  and and_3 (and_3_out, and_1_out, D);
  nor nor_1 (nor_1_out, and_2_out, nor_2_out);
  nor nor_2 (nor_2_out, nor_1_out, and_3_out);
  assign Q = OE ? nor_1_out : 1'bz;  // Controlled_Buffer controlled_buffer_1
endmodule

module register16 (
  input  CLK,
  input  WE,
  input  [15:0] D_IN,
  input  OE,
  output [15:0] D_OUT
);

  register8 register8_1 (.D_OUT(D_OUT[7:0]), .CLK(CLK), .OE(OE), .WE(WE), .D_IN(D_IN[7:0]));
  register8 register8_2 (.D_OUT(D_OUT[15:8]), .CLK(CLK), .OE(OE), .WE(WE), .D_IN(D_IN[15:8]));
endmodule

module RegisterFile16 (
  input  [3:0] read_addr1,
  input  [3:0] read_addr2,
  input  [15:0] data_in,
  input  [3:0] write_addr,
  input  LD,
  output [15:0] data_out1,
  output [15:0] data_out2
);

  wire decoder4x16_1_p1, decoder4x16_1_p2, decoder4x16_1_p3, decoder4x16_1_p4, decoder4x16_1_p5,
       decoder4x16_1_p6, decoder4x16_1_p7, decoder4x16_1_p8, decoder4x16_1_p9, decoder4x16_1_p10;
  wire [15:0] register16_1_d_out, register16_2_d_out, register16_3_d_out, register16_4_d_out,
       register16_5_d_out, register16_6_d_out, register16_7_d_out, register16_8_d_out, register16_9_d_out,
       register16_10_d_out, register16_11_d_out, register16_12_d_out, register16_13_d_out,
       register16_14_d_out, register16_15_d_out, register16_16_d_out;

  // decoder4x16 decoder4x16_1: pin names not known; wires that end beside it: decoder4x16_1_p1, decoder4x16_1_p2, decoder4x16_1_p3, decoder4x16_1_p4, decoder4x16_1_p5, decoder4x16_1_p6, decoder4x16_1_p7, decoder4x16_1_p8, decoder4x16_1_p9, decoder4x16_1_p10
  register16 register16_1 (.D_OUT(register16_1_d_out));  // open: WE, D_IN, CLK, OE
  register16 register16_2 (.D_OUT(register16_2_d_out));  // open: WE, D_IN, CLK, OE
  register16 register16_3 (.D_OUT(register16_3_d_out));  // open: WE, D_IN, CLK, OE
  register16 register16_4 (.D_OUT(register16_4_d_out));  // open: WE, D_IN, CLK, OE
  register16 register16_5 (.D_OUT(register16_5_d_out));  // open: WE, D_IN, CLK, OE
  register16 register16_6 (.D_OUT(register16_6_d_out));  // open: WE, D_IN, CLK, OE
  register16 register16_7 (.D_OUT(register16_7_d_out));  // open: WE, D_IN, CLK, OE
  register16 register16_8 (.D_OUT(register16_8_d_out));  // open: WE, D_IN, CLK, OE
  register16 register16_9 (.D_OUT(register16_9_d_out));  // open: WE, D_IN, CLK, OE
  register16 register16_10 (.D_OUT(register16_10_d_out));  // open: WE, D_IN, CLK, OE
  register16 register16_11 (.D_OUT(register16_11_d_out));  // open: WE, D_IN, CLK, OE
  register16 register16_12 (.D_OUT(register16_12_d_out));  // open: WE, D_IN, CLK, OE
  register16 register16_13 (.D_OUT(register16_13_d_out));  // open: WE, D_IN, CLK, OE
  register16 register16_14 (.D_OUT(register16_14_d_out));  // open: WE, D_IN, CLK, OE
  register16 register16_15 (.D_OUT(register16_15_d_out));  // open: WE, D_IN, CLK, OE
  register16 register16_16 (.D_OUT(register16_16_d_out));  // open: WE, D_IN, CLK, OE
  multiplexer16x1 multiplexer16x1_1 (.out_18(data_out1));  // open: addr_in, IN_0, IN_1, IN_2, IN_3, IN_4, IN_5, IN_6, IN_7, IN_8, IN_9, IN_10, IN_11, IN_12, IN_13, IN_14, IN_15
  multiplexer16x1 multiplexer16x1_2 (.out_18(data_out2));  // open: addr_in, IN_0, IN_1, IN_2, IN_3, IN_4, IN_5, IN_6, IN_7, IN_8, IN_9, IN_10, IN_11, IN_12, IN_13, IN_14, IN_15
endmodule

module demultiplexer16_1x8 (
  input  [15:0] DataIn,
  input  [2:0] Addr,
  output [15:0] out_3,
  output [15:0] out_4,
  output [15:0] out_5,
  output [15:0] out_6,
  output [15:0] out_7,
  output [15:0] out_8,
  output [15:0] out_9,
  output [15:0] out_10
);

  wire decoder_8_1_out_0, decoder_8_1_out_1, decoder_8_1_out_2, decoder_8_1_out_3, decoder_8_1_out_4,
       decoder_8_1_out_5, decoder_8_1_out_6, decoder_8_1_out_7;

  decoder_8 decoder_8_1 (
    .IN_A(Addr), .Out_0(decoder_8_1_out_0), .Out_1(decoder_8_1_out_1), .Out_2(decoder_8_1_out_2),
    .Out_3(decoder_8_1_out_3), .Out_4(decoder_8_1_out_4), .Out_5(decoder_8_1_out_5),
    .Out_6(decoder_8_1_out_6), .Out_7(decoder_8_1_out_7));  // open: Clk
  assign out_3 = decoder_8_1_out_0 ? DataIn : 16'bz;  // Controlled_Buffer controlled_buffer_1
  assign out_4 = decoder_8_1_out_1 ? DataIn : 16'bz;  // Controlled_Buffer controlled_buffer_2
  assign out_5 = decoder_8_1_out_2 ? DataIn : 16'bz;  // Controlled_Buffer controlled_buffer_3
  assign out_6 = decoder_8_1_out_3 ? DataIn : 16'bz;  // Controlled_Buffer controlled_buffer_4
  assign out_7 = decoder_8_1_out_4 ? DataIn : 16'bz;  // Controlled_Buffer controlled_buffer_5
  assign out_8 = decoder_8_1_out_5 ? DataIn : 16'bz;  // Controlled_Buffer controlled_buffer_6
  assign out_9 = decoder_8_1_out_6 ? DataIn : 16'bz;  // Controlled_Buffer controlled_buffer_7
  assign out_10 = decoder_8_1_out_7 ? DataIn : 16'bz;  // Controlled_Buffer controlled_buffer_8
endmodule

module program_counter (
  input  [2:0] IN_PC,
  input  EN,
  output [2:0] OUT_PC
);

  // d_flip_flop d_flip_flop_1: pin names not known; wires that end beside it: OUT_PC[2], OUT_PC[1]
  // d_flip_flop d_flip_flop_2: pin names not known; wires that end beside it: OUT_PC[2], OUT_PC[1], OUT_PC[0]
  // d_flip_flop d_flip_flop_3: pin names not known; wires that end beside it: OUT_PC[1], OUT_PC[0]
endmodule

module instruction_memory (
  input  [3:0] read_addr1,
  input  [3:0] write_addr,
  output [15:0] data_out1
);

  wire [15:0] multiplexer16x1_1_p2;

  // multiplexer16x1 multiplexer16x1_1: pin names not known; wires that end beside it: read_addr1, multiplexer16x1_1_p2
  RegisterFile16 registerfile16_1 (
    .read_addr1(read_addr1), .data_in(multiplexer16x1_1_p2), .write_addr(write_addr), .LD(1'b1),
    .data_out1(data_out1));  // open: read_addr2, data_out2
endmodule

module multiplexer16x1 (
  input  [15:0] IN_0,
  input  [15:0] IN_1,
  input  [15:0] IN_2,
  input  [15:0] IN_3,
  input  [15:0] IN_4,
  input  [15:0] IN_5,
  input  [15:0] IN_6,
  input  [15:0] IN_7,
  input  [15:0] IN_8,
  input  [15:0] IN_9,
  input  [15:0] IN_10,
  input  [15:0] IN_11,
  input  [15:0] IN_12,
  input  [15:0] IN_13,
  input  [15:0] IN_14,
  input  [15:0] IN_15,
  input  [3:0] addr_in,
  output [15:0] out_18
);

  wire decoder4x16_1_out_0, decoder4x16_1_out_1, decoder4x16_1_out_2, decoder4x16_1_out_3,
       decoder4x16_1_out_4, decoder4x16_1_out_5, decoder4x16_1_out_6, decoder4x16_1_out_7,
       decoder4x16_1_out_8, decoder4x16_1_out_9, decoder4x16_1_out_10, decoder4x16_1_out_11,
       decoder4x16_1_out_12, decoder4x16_1_out_13, decoder4x16_1_out_14, decoder4x16_1_out_15;

  decoder4x16 decoder4x16_1 (
    .Out_0(decoder4x16_1_out_0), .Out_12(decoder4x16_1_out_12), .Out_13(decoder4x16_1_out_13),
    .Out_14(decoder4x16_1_out_14), .Out_15(decoder4x16_1_out_15), .Out_1(decoder4x16_1_out_1),
    .Out_2(decoder4x16_1_out_2), .Out_3(decoder4x16_1_out_3), .Out_4(decoder4x16_1_out_4),
    .Out_5(decoder4x16_1_out_5), .Out_6(decoder4x16_1_out_6), .Out_7(decoder4x16_1_out_7),
    .Out_8(decoder4x16_1_out_8), .Out_9(decoder4x16_1_out_9), .Out_10(decoder4x16_1_out_10),
    .Out_11(decoder4x16_1_out_11), .Addr(addr_in));
  assign out_18 = decoder4x16_1_out_0 ? IN_0 : 16'bz;  // Controlled_Buffer controlled_buffer_1
  assign out_18 = decoder4x16_1_out_1 ? IN_1 : 16'bz;  // Controlled_Buffer controlled_buffer_2
  assign out_18 = decoder4x16_1_out_2 ? IN_2 : 16'bz;  // Controlled_Buffer controlled_buffer_3
  assign out_18 = decoder4x16_1_out_3 ? IN_3 : 16'bz;  // Controlled_Buffer controlled_buffer_4
  assign out_18 = decoder4x16_1_out_4 ? IN_4 : 16'bz;  // Controlled_Buffer controlled_buffer_5
  assign out_18 = decoder4x16_1_out_5 ? IN_5 : 16'bz;  // Controlled_Buffer controlled_buffer_6
  assign out_18 = decoder4x16_1_out_6 ? IN_6 : 16'bz;  // Controlled_Buffer controlled_buffer_7
  assign out_18 = decoder4x16_1_out_7 ? IN_7 : 16'bz;  // Controlled_Buffer controlled_buffer_8
  assign out_18 = decoder4x16_1_out_8 ? IN_8 : 16'bz;  // Controlled_Buffer controlled_buffer_9
  assign out_18 = decoder4x16_1_out_9 ? IN_9 : 16'bz;  // Controlled_Buffer controlled_buffer_10
  assign out_18 = decoder4x16_1_out_10 ? IN_10 : 16'bz;  // Controlled_Buffer controlled_buffer_11
  assign out_18 = decoder4x16_1_out_11 ? IN_11 : 16'bz;  // Controlled_Buffer controlled_buffer_12
  assign out_18 = decoder4x16_1_out_12 ? IN_12 : 16'bz;  // Controlled_Buffer controlled_buffer_13
  assign out_18 = decoder4x16_1_out_13 ? IN_13 : 16'bz;  // Controlled_Buffer controlled_buffer_14
  assign out_18 = decoder4x16_1_out_14 ? IN_14 : 16'bz;  // Controlled_Buffer controlled_buffer_15
  assign out_18 = decoder4x16_1_out_15 ? IN_15 : 16'bz;  // Controlled_Buffer controlled_buffer_16
endmodule

module decoder4x16 (
  input  [3:0] Addr,
  output Out_0,
  output Out_1,
  output Out_2,
  output Out_3,
  output Out_4,
  output Out_5,
  output Out_6,
  output Out_7,
  output Out_8,
  output Out_9,
  output Out_10,
  output Out_11,
  output Out_12,
  output Out_13,
  output Out_14,
  output Out_15
);

  and and_1 (Out_0, ~Addr[0], ~Addr[1], ~Addr[2], ~Addr[3]);  // AND_Gate
  and and_2 (Out_1, Addr[0], ~Addr[1], ~Addr[2], ~Addr[3]);  // AND_Gate
  and and_3 (Out_2, ~Addr[0], Addr[1], ~Addr[2], ~Addr[3]);  // AND_Gate
  and and_4 (Out_3, Addr[0], Addr[1], ~Addr[2], ~Addr[3]);  // AND_Gate
  and and_5 (Out_4, ~Addr[0], ~Addr[1], Addr[2], ~Addr[3]);  // AND_Gate
  and and_6 (Out_5, Addr[0], ~Addr[1], Addr[2], ~Addr[3]);  // AND_Gate
  and and_7 (Out_6, ~Addr[0], Addr[1], Addr[2], ~Addr[3]);  // AND_Gate
  and and_8 (Out_7, Addr[0], Addr[1], Addr[2], ~Addr[3]);  // AND_Gate
  and and_9 (Out_8, ~Addr[0], ~Addr[1], ~Addr[2], Addr[3]);  // AND_Gate
  and and_10 (Out_9, Addr[0], ~Addr[1], ~Addr[2], Addr[3]);  // AND_Gate
  and and_11 (Out_10, ~Addr[0], Addr[1], ~Addr[2], Addr[3]);  // AND_Gate
  and and_12 (Out_11, Addr[0], Addr[1], ~Addr[2], Addr[3]);  // AND_Gate
  and and_13 (Out_12, ~Addr[0], ~Addr[1], Addr[2], Addr[3]);  // AND_Gate
  and and_14 (Out_13, Addr[0], ~Addr[1], Addr[2], Addr[3]);  // AND_Gate
  and and_15 (Out_14, ~Addr[0], Addr[1], Addr[2], Addr[3]);  // AND_Gate
  and and_16 (Out_15, Addr[0], Addr[1], Addr[2], Addr[3]);
endmodule

module data_memory (
  input  [3:0] in_1,
  output [15:0] out_2
);

  multiplexer16x1 multiplexer16x1_1 (.out_18(out_2));  // open: addr_in, IN_0, IN_1, IN_2, IN_3, IN_4, IN_5, IN_6, IN_7, IN_8, IN_9, IN_10, IN_11, IN_12, IN_13, IN_14, IN_15
endmodule

module RAM_1Kx16 (
  input  [7:0] addr_in,
  input  EN,
  input  LD,
  input  Clk,
  input  [15:0] data_in,
  output [15:0] data_out
);

  RAM #(.dataWidth(16)) ram_1 (.addr(addr_in), .we(EN), .oe(LD), .clk(Clk), .din(data_in), .dout(data_out));
endmodule

module multiplexer2_1 (
  input  addr_in
);

  decoder1x2 decoder1x2_1 (.addr_in(addr_in));  // open: out_0, out_1
endmodule

module decoder1x2 (
  input  addr_in,
  output out_0,
  output out_1
);

  and and_1 (out_0, ~addr_in, 1'b1);  // AND_Gate
  and and_2 (out_1, addr_in, 1'b1);
endmodule

module register8 (
  input  CLK,
  input  WE,
  input  [7:0] D_IN,
  input  OE,
  output [7:0] D_OUT
);

  d_flip_flop d_flip_flop_1 (.Q(D_OUT[0]), .WE(WE), .CLK(CLK), .D(D_IN[0]), .OE(OE));
  d_flip_flop d_flip_flop_2 (.Q(D_OUT[1]), .WE(WE), .CLK(CLK), .D(D_IN[1]), .OE(OE));
  d_flip_flop d_flip_flop_3 (.Q(D_OUT[2]), .WE(WE), .CLK(CLK), .D(D_IN[2]), .OE(OE));
  d_flip_flop d_flip_flop_4 (.Q(D_OUT[3]), .WE(WE), .CLK(CLK), .D(D_IN[3]), .OE(OE));
  d_flip_flop d_flip_flop_5 (.Q(D_OUT[4]), .WE(WE), .CLK(CLK), .D(D_IN[4]), .OE(OE));
  d_flip_flop d_flip_flop_6 (.Q(D_OUT[5]), .WE(WE), .CLK(CLK), .D(D_IN[5]), .OE(OE));
  d_flip_flop d_flip_flop_7 (.Q(D_OUT[6]), .WE(WE), .CLK(CLK), .D(D_IN[6]), .OE(OE));
  d_flip_flop d_flip_flop_8 (.Q(D_OUT[7]), .WE(WE), .CLK(CLK), .D(D_IN[7]), .OE(OE));
endmodule

module memory (
  input  [15:0] D_IN,
  input  [3:0] WriteAddr,
  input  [3:0] ReadAddr1,
  input  WE,
  input  CLK,
  input  [3:0] ReadAddr2,
  input  OE,
  output [15:0] D_OUT1,
  output [15:0] D_OUT2
);

  wire and_1_out, and_2_out, and_3_out, and_4_out, and_5_out, and_6_out, and_7_out, and_8_out, and_9_out,
       and_10_out, and_11_out, and_12_out, and_13_out, and_14_out, and_15_out, and_16_out,
       decoder4x16_1_out_0, decoder4x16_1_out_1, decoder4x16_1_out_2, decoder4x16_1_out_3,
       decoder4x16_1_out_4, decoder4x16_1_out_5, decoder4x16_1_out_6, decoder4x16_1_out_7,
       decoder4x16_1_out_8, decoder4x16_1_out_9, decoder4x16_1_out_10, decoder4x16_1_out_11,
       decoder4x16_1_out_12, decoder4x16_1_out_13, decoder4x16_1_out_14, decoder4x16_1_out_15;
  wire [15:0] register16_1_d_out, register16_2_d_out, register16_3_d_out, register16_4_d_out,
       register16_5_d_out, register16_6_d_out, register16_7_d_out, register16_8_d_out, register16_9_d_out,
       register16_10_d_out, register16_11_d_out, register16_12_d_out, register16_13_d_out,
       register16_14_d_out, register16_15_d_out, register16_16_d_out;

  decoder4x16 decoder4x16_1 (
    .Out_0(decoder4x16_1_out_0), .Out_12(decoder4x16_1_out_12), .Out_13(decoder4x16_1_out_13),
    .Out_14(decoder4x16_1_out_14), .Out_15(decoder4x16_1_out_15), .Out_1(decoder4x16_1_out_1),
    .Out_2(decoder4x16_1_out_2), .Out_3(decoder4x16_1_out_3), .Out_4(decoder4x16_1_out_4),
    .Out_5(decoder4x16_1_out_5), .Out_6(decoder4x16_1_out_6), .Out_7(decoder4x16_1_out_7),
    .Out_8(decoder4x16_1_out_8), .Out_9(decoder4x16_1_out_9), .Out_10(decoder4x16_1_out_10),
    .Out_11(decoder4x16_1_out_11), .Addr(WriteAddr));
  and and_1 (and_1_out, WE, decoder4x16_1_out_3);
  and and_2 (and_2_out, WE, decoder4x16_1_out_7);
  and and_3 (and_3_out, WE, decoder4x16_1_out_11);
  and and_4 (and_4_out, WE, decoder4x16_1_out_15);
  register16 register16_1 (.D_OUT(register16_1_d_out), .WE(and_1_out), .D_IN(D_IN), .CLK(CLK), .OE(OE));
  register16 register16_2 (.D_OUT(register16_2_d_out), .WE(and_2_out), .D_IN(D_IN), .CLK(CLK), .OE(OE));
  register16 register16_3 (.D_OUT(register16_3_d_out), .WE(and_3_out), .D_IN(D_IN), .CLK(CLK), .OE(OE));
  register16 register16_4 (.D_OUT(register16_4_d_out), .WE(and_4_out), .D_IN(D_IN), .CLK(CLK), .OE(OE));
  and and_5 (and_5_out, WE, decoder4x16_1_out_2);
  register16 register16_5 (.D_OUT(register16_5_d_out), .WE(and_5_out), .D_IN(D_IN), .CLK(CLK), .OE(OE));
  and and_6 (and_6_out, WE, decoder4x16_1_out_6);
  register16 register16_6 (.D_OUT(register16_6_d_out), .WE(and_6_out), .D_IN(D_IN), .CLK(CLK), .OE(OE));
  and and_7 (and_7_out, WE, decoder4x16_1_out_10);
  register16 register16_7 (.D_OUT(register16_7_d_out), .WE(and_7_out), .D_IN(D_IN), .CLK(CLK), .OE(OE));
  and and_8 (and_8_out, WE, decoder4x16_1_out_14);
  register16 register16_8 (.D_OUT(register16_8_d_out), .WE(and_8_out), .D_IN(D_IN), .CLK(CLK), .OE(OE));
  and and_9 (and_9_out, WE, decoder4x16_1_out_1);
  register16 register16_9 (.D_OUT(register16_9_d_out), .WE(and_9_out), .D_IN(D_IN), .CLK(CLK), .OE(OE));
  and and_10 (and_10_out, WE, decoder4x16_1_out_5);
  register16 register16_10 (.D_OUT(register16_10_d_out), .WE(and_10_out), .D_IN(D_IN), .CLK(CLK), .OE(OE));
  and and_11 (and_11_out, WE, decoder4x16_1_out_9);
  register16 register16_11 (.D_OUT(register16_11_d_out), .WE(and_11_out), .D_IN(D_IN), .CLK(CLK), .OE(OE));
  and and_12 (and_12_out, WE, decoder4x16_1_out_13);
  register16 register16_12 (.D_OUT(register16_12_d_out), .WE(and_12_out), .D_IN(D_IN), .CLK(CLK), .OE(OE));
  and and_13 (and_13_out, WE, decoder4x16_1_out_0);
  register16 register16_13 (.D_OUT(register16_13_d_out), .WE(and_13_out), .D_IN(D_IN), .CLK(CLK), .OE(OE));
  and and_14 (and_14_out, WE, decoder4x16_1_out_4);
  register16 register16_14 (.D_OUT(register16_14_d_out), .WE(and_14_out), .D_IN(D_IN), .CLK(CLK), .OE(OE));
  and and_15 (and_15_out, WE, decoder4x16_1_out_8);
  register16 register16_15 (.D_OUT(register16_15_d_out), .WE(and_15_out), .D_IN(D_IN), .CLK(CLK), .OE(OE));
  and and_16 (and_16_out, WE, decoder4x16_1_out_12);
  register16 register16_16 (.D_OUT(register16_16_d_out), .WE(and_16_out), .D_IN(D_IN), .CLK(CLK), .OE(OE));
  multiplexer16x1 multiplexer16x1_1 (
    .out_18(D_OUT1), .addr_in(ReadAddr1), .IN_0(register16_13_d_out), .IN_1(register16_9_d_out),
    .IN_2(register16_5_d_out), .IN_3(register16_1_d_out), .IN_4(register16_14_d_out),
    .IN_5(register16_10_d_out), .IN_6(register16_6_d_out), .IN_7(register16_2_d_out),
    .IN_8(register16_15_d_out), .IN_9(register16_11_d_out), .IN_10(register16_7_d_out),
    .IN_11(register16_3_d_out), .IN_12(register16_16_d_out), .IN_13(register16_12_d_out),
    .IN_14(register16_8_d_out), .IN_15(register16_4_d_out));
  multiplexer16x1 multiplexer16x1_2 (
    .out_18(D_OUT2), .addr_in(ReadAddr2), .IN_0(register16_13_d_out), .IN_1(register16_9_d_out),
    .IN_2(register16_5_d_out), .IN_3(register16_1_d_out), .IN_4(register16_14_d_out),
    .IN_5(register16_10_d_out), .IN_6(register16_6_d_out), .IN_7(register16_2_d_out),
    .IN_8(register16_15_d_out), .IN_9(register16_11_d_out), .IN_10(register16_7_d_out),
    .IN_11(register16_3_d_out), .IN_12(register16_16_d_out), .IN_13(register16_12_d_out),
    .IN_14(register16_8_d_out), .IN_15(register16_4_d_out));
endmodule
